# Fritzing sketch Circuito (saved by Fritzing 0.9.3b)
circuit board: 6.88566cm x 5.36311cm
breadboards: 2

parts:
  Componente1 = Arduino Uno (Rev3)
  R11 = Resistor [tolerance=±5% resistance=3.9M package="0805 [SMD]"]
  R6 = Resistor [tolerance=±5% resistance=3.9M package="0805 [SMD]"]
  R10 = Resistor [tolerance=±5% resistance=3.9M package="0805 [SMD]"]
  R12 = Resistor [tolerance=±5% resistance=3.9M package="0805 [SMD]"]
  R7 = Resistor [tolerance=±5% resistance=10k package="0805 [SMD]"]
  U1 = POT [package=alps_pot]
  R13 = Resistor [tolerance=±5% resistance=300 package="0805 [SMD]"]
  D1 = Zener Diode [part_number=1N4732A breakdown_voltage=5.1V package="Melf DO-213 AB [SMD]"]
  Cursors = Pushbutton [package=THT]
  C1 = Ceramic Capacitor [capacitance=10nF package="0805 [SMD, multilayer]"]
  Cursors1 = Pushbutton [package=THT]
  R14 = Resistor [tolerance=±5% resistance=10k package="0805 [SMD]"]
  C2 = Ceramic Capacitor [capacitance=10nF package="0805 [SMD, multilayer]"]
  Cursors2 = Pushbutton [package=THT]
  R15 = Resistor [tolerance=±5% resistance=10k package="0805 [SMD]"]
  C3 = Ceramic Capacitor [capacitance=10nF package="0805 [SMD, multilayer]"]
  Cursors3 = Pushbutton [package=THT]
  R16 = Resistor [tolerance=±5% resistance=10k package="0805 [SMD]"]
  C4 = Ceramic Capacitor [capacitance=10nF package="0805 [SMD, multilayer]"]

nets (from the breadboard view):
  N1: Componente1.A0, Componente1.GND, R11.Pin_1, R6.Pin_1, R10.Pin_1, R12.Pin_1, U1.A, D1.anode, Cursors.leg1, C1.0, Cursors1.leg1, C2.0, Cursors2.leg1, C3.0, Cursors3.leg1, C4.0
  N2: Componente1.A1, R6.Pin_0, R13.Pin_1, D1.cathode
  N3: Componente1.A2, R10.Pin_0
  N4: Componente1.A3, R11.Pin_0
  N5: Componente1.A4/SDA, R12.Pin_0
  N6: Componente1.A5/SCL, U1.S
  N7: Componente1.5V, R7.Pin_1, U1.E, R14.Pin_1, R15.Pin_1, R16.Pin_1
  N8: R7.Pin_0, Cursors.leg0, C1.1
  N9: Cursors1.leg0, R14.Pin_0, C2.1
  N10: Cursors2.leg0, R15.Pin_0, C3.1
  N11: Cursors3.leg0, R16.Pin_0, C4.1
